# Fritzing sketch chrono_display_0_2 (saved by Fritzing 0.7.7b)

parts:
  Arduino1 = Arduino
  Composants1 = Arduino Xbee Libellium Shield
  U1 = XBee
  LCD1 = LCD screen
  R1 = Rotary Potentiometer (Small) [maximum_resistance=100kΩ]

nets:
  N1: Arduino1.D13, LCD1.RS
  N2: Arduino1.D10, LCD1.E
  N3: Arduino1.+5V, Composants1.DOUT, U1.pin2
  N4: Composants1.D2, LCD1.DB7
  N5: Composants1.D3, LCD1.DB6
  N6: Composants1.D4, LCD1.DB5
  N7: Composants1.D5, LCD1.DB4
  N8: Composants1.I/08, U1.pin20
  N9: Composants1.I/02, U1.pin19
  N10: Composants1.I/03, U1.pin18
  N11: Composants1.I/06, U1.pin17
  N12: Composants1.I/05, U1.pin16
  N13: Composants1.15, U1.pin15
  N14: Composants1.14, U1.pin14
  N15: Composants1.13, U1.pin13
  N16: Composants1.I/07, U1.pin12
  N17: Composants1.I/04, U1.pin11
  +5V: Composants1.+5V, LCD1.VDD, R1.leg2
  GND: Composants1.GND, U1.GND, LCD1.VSS, LCD1.DB1, R1.leg1
  N18: Composants1.9, U1.pin9
  N19: Composants1.8, U1.pin8
  N20: Composants1.PWM1, U1.pin7
  N21: Composants1.PWM0, U1.pin6
  N22: Composants1.RST, U1.pin5
  N23: Composants1.4, U1.pin4
  N24: Composants1.DIN, U1.pin3
  +3V3: Composants1.+3V3, U1.VCC
  N25: LCD1.V0, R1.wiper

notes:
  An Arduino Leonardo with an XBee Shield and an XBee Pro (Serie 1)
  Potentiometer
