# Fritzing sketch chrono_sensor_0_2 (saved by Fritzing 0.7.7b)
breadboards: 1

parts:
  Arduino1 = Arduino  # not connected
  Composants1 = Arduino Xbee Libellium Shield
  Q1 = NPN-Transistor [package="TO92 [THT]"]
  LED1 = LED - 5mm [color="Red (633nm)" package="5 mm [THT]"]
  R1 = Resistor [tolerance=±5% resistance=220 package=THT]
  LED2 = LED - 5mm [color="Red (633nm)" package="5 mm [THT]"]
  LED3 = LED - 5mm [color="Red (633nm)" package="5 mm [THT]"]

nets:
  N1: Composants1.GND, Q1.B, LED3.cathode
  N2: Composants1.D2, Q1.E
  N3: Composants1.+5V, Q1.C, R1.Pin_1
  N4: LED1.cathode, LED2.anode
  N5: LED1.anode, R1.Pin_0
  N6: LED2.cathode, LED3.anode

notes:
  IR LEDs
  IR Sensor
  Arduino + XBee Shield + XBee
