# Fritzing sketch laser_standalone (saved by Fritzing 0.7.7b)
breadboards: 1

parts:
  VCC1 = Battery
  S1 = Toggle Switch [package=THT]
  LED1 = LED - 5mm [color="Red (633nm)" package="5 mm [THT]"]
  VCC2 = Battery

nets:
  N1: VCC1.-, S1.L2, LED1.anode, VCC2.-
  N2: VCC1.+, S1.L1, S1.COM, LED1.cathode, VCC2.+

notes:
  Panneau solaire
